// Logisim project varianta_finala_v5.circ as structural Verilog
module UE (
  input  [3:0] DATA_IN,
  input  RESET_BUTTON,
  input  CLK,
  output AVAILABLE,
  output [6:0] SSD_FIRST,
  output [6:0] SSD_SECOND,
  output [6:0] SSD_THIRD,
  output BLOCKED
);

  wire and_1_out, and_2_out, and_3_out, b00e_out, b00i_out, b01e_out, b01i_out, b10e_out, b10i_out,
       CHECKED_out, comparator_1_lt, comparator_triple_4b_1_equality, counter_2_carry, d_ff_1_q, d_ff_2_q,
       d_ff_4_q, end_eval_out, end_init_out, RESET, RESET_2, second_start_init_out;
  wire [0:0] SSD_0;
  wire [1:0] counter_1_q, counter_2_q, counter_3_q;
  wire [1:1] d_ff_3_q;
  wire [3:0] FIRST_REG_BIN_EVAL, FIRST_REG_BIN_INIT, SECOND_REG_BIN_EVAL, SECOND_REG_BIN_INIT,
       THIRD_REG_BIN_EVAL, THIRD_REG_BIN_INIT;
  wire [6:0] FIRST_REG_DATA_EVAL, FIRST_REG_DATA_INIT, SECOND_REG_DATA_EVAL, SECOND_REG_DATA_INIT,
       THIRD_REG_DATA_EVAL, THIRD_REG_DATA_INIT;

  D_Flip_Flop d_ff_1 (.D(CHECKED_out), .clk(CLK), .Q(d_ff_1_q), .reset(RESET));  // open: Qn, preset
  or or_1 (RESET_2, RESET, d_ff_2_q);
  D_Flip_Flop d_ff_2 (.D(and_1_out), .clk(CLK), .Q(d_ff_2_q), .reset(RESET));  // open: Qn, preset
  or or_2 (RESET, RESET_BUTTON, d_ff_1_q);
  and and_1 (and_1_out, and_2_out, comparator_1_lt);
  not not_1 (SSD_0[0], 1'b1);
  Counter #(.max('h3), .ongoal("stay"), .trigger("falling"), .width(2)) counter_1 (
    .clr(RESET), .load(1'b0), .up(1'b1), .count(1'b1), .clk(CLK), .D(2'b00), .carry(AVAILABLE),
    .Q(counter_1_q));
  D_Flip_Flop d_ff_3 (.D(AVAILABLE), .clk(CLK), .Q(d_ff_3_q[1]), .reset(RESET));  // open: Qn, preset
  Counter #(.max('h3), .ongoal("stay"), .width(2)) counter_2 (
    .clr(RESET_2), .load(1'b0), .up(d_ff_3_q[1]), .count(d_ff_3_q[1]), .clk(CLK), .D(2'b00),
    .carry(counter_2_carry), .Q(counter_2_q));
  Counter #(.max('h3), .trigger("falling"), .width(2)) counter_3 (
    .clr(RESET), .load(RESET), .up(1'b1), .count(1'b1), .clk(and_2_out), .D(2'b00), .carry(BLOCKED),
    .Q(counter_3_q));
  and CHECKED (CHECKED_out, ~BLOCKED, AVAILABLE, comparator_triple_4b_1_equality);  // AND_Gate
  and and_2 (and_2_out, ~comparator_triple_4b_1_equality, and_3_out);  // AND_Gate
  Comparator #(.mode("unsigned"), .width(2)) comparator_1 (
    .a(counter_3_q), .b(2'b11), .lt(comparator_1_lt));  // open: gt, eq
  and b00i (b00i_out, ~counter_1_q[0], ~counter_1_q[1], 1'b1);  // AND_Gate
  and b01i (b01i_out, counter_1_q[0], ~counter_1_q[1], 1'b1);  // AND_Gate
  and b10i (b10i_out, ~counter_1_q[0], counter_1_q[1], 1'b1);  // AND_Gate
  and and_3 (and_3_out, d_ff_4_q, ~BLOCKED);  // AND_Gate
  and b00e (b00e_out, ~counter_2_q[0], ~counter_2_q[1], 1'b1);  // AND_Gate
  and b01e (b01e_out, counter_2_q[0], ~counter_2_q[1], 1'b1);  // AND_Gate
  and b10e (b10e_out, ~counter_2_q[0], counter_2_q[1], 1'b1);  // AND_Gate
  D_Flip_Flop d_ff_4 (.D(end_eval_out), .clk(CLK), .Q(d_ff_4_q), .reset(RESET));  // open: Qn, preset
  and end_init (end_init_out, b10i_out, ~AVAILABLE);  // AND_Gate
  and second_start_init (second_start_init_out, d_ff_3_q[1], b00e_out);
  and end_eval (end_eval_out, b10e_out, ~counter_2_carry);  // AND_Gate
  custom_register u_FIRST_REG_DATA_INIT (
    .DATA_IN(DATA_IN), .ENABLE(b00i_out), .CLOCK(CLK), .RESET(RESET), .SSD_ENCODING(FIRST_REG_DATA_INIT),
    .DATA(FIRST_REG_BIN_INIT));
  custom_register u_SECOND_REG_DATA_INIT (
    .DATA_IN(DATA_IN), .ENABLE(b01i_out), .CLOCK(CLK), .RESET(RESET), .SSD_ENCODING(SECOND_REG_DATA_INIT),
    .DATA(SECOND_REG_BIN_INIT));
  custom_register u_THIRD_REG_DATA_INIT (
    .DATA_IN(DATA_IN), .ENABLE(end_init_out), .CLOCK(CLK), .RESET(RESET), .SSD_ENCODING(THIRD_REG_DATA_INIT),
    .DATA(THIRD_REG_BIN_INIT));
  custom_register u_FIRST_REG_DATA_EVAL (
    .DATA_IN(DATA_IN), .ENABLE(second_start_init_out), .CLOCK(CLK), .RESET(RESET_2),
    .SSD_ENCODING(FIRST_REG_DATA_EVAL), .DATA(FIRST_REG_BIN_EVAL));
  custom_register u_SECOND_REG_DATA_EVAL (
    .DATA_IN(DATA_IN), .ENABLE(b01e_out), .CLOCK(CLK), .RESET(RESET_2), .SSD_ENCODING(SECOND_REG_DATA_EVAL),
    .DATA(SECOND_REG_BIN_EVAL));
  custom_register u_THIRD_REG_DATA_EVAL (
    .DATA_IN(DATA_IN), .ENABLE(end_eval_out), .CLOCK(CLK), .RESET(RESET_2),
    .SSD_ENCODING(THIRD_REG_DATA_EVAL), .DATA(THIRD_REG_BIN_EVAL));
  triple_ssd_with_3_outputs triple_ssd_with_3_outputs_1 (
    .FIRST_FIRST(FIRST_REG_DATA_INIT), .FIRST_SECOND({{6{1'b1}}, SSD_0[0]}),
    .FIRST_THIRD(FIRST_REG_DATA_EVAL), .SECOND_FIRST(SECOND_REG_DATA_INIT),
    .SECOND_SECOND({{6{1'b1}}, SSD_0[0]}), .SECOND_THIRD(SECOND_REG_DATA_EVAL),
    .THIRD_FIRST(THIRD_REG_DATA_INIT), .THIRD_SECOND({{6{1'b1}}, SSD_0[0]}),
    .THIRD_THIRD(THIRD_REG_DATA_EVAL), .SELECTOR({d_ff_3_q[1], AVAILABLE}), .FIRST_SSD_OUTPUT(SSD_FIRST),
    .SECOND_SSD_OUTPUT(SSD_SECOND), .THIRD_SSD_OUTPUT(SSD_THIRD));
  comparator_triple_4b comparator_triple_4b_1 (
    .FIRST_A(FIRST_REG_BIN_INIT), .FIRST_B(FIRST_REG_BIN_EVAL), .SECOND_A(SECOND_REG_BIN_INIT),
    .SECOND_B(SECOND_REG_BIN_EVAL), .THIRD_A(THIRD_REG_BIN_INIT), .THIRD_B(THIRD_REG_BIN_EVAL),
    .ENABLE(counter_2_carry), .EQUALITY(comparator_triple_4b_1_equality));

  // Other names for the same wires on the sheet: CLOCK = CLK

  // Notes on the sheet:
  //   LED care arata daca s-a blocat dulapul
  //   Output pentru LEDul de disponibilitate.
  //   3 incercari pentru cod, sau locker-ul se blocheaza
  //   Datele de intrare initiale.
  //   Date de intrare pentru evaluarea celor initiale
endmodule

// REG_DATA_SSDENC
module custom_register (
  input  [3:0] DATA_IN,
  input  ENABLE,
  input  CLOCK,
  input  RESET,
  output [6:0] SSD_ENCODING,
  output [3:0] DATA
);

  Register #(.width(4)) register_1 (.D(DATA_IN), .en(ENABLE), .clk(CLOCK), .Q(DATA), .clr(RESET));
  hex_to_7seg hex_to_7seg_1 (.hex_in(DATA), .a_b_c_d_e_f_g(SSD_ENCODING));
endmodule

module comparator_4b (
  input  [3:0] DATA_A,
  input  [3:0] DATA_B,
  output RESULT
);

  wire xnor_1_out, xnor_2_out, xnor_3_out, xnor_4_out;

  xnor xnor_1 (xnor_1_out, DATA_A[0], DATA_B[0]);
  xnor xnor_2 (xnor_2_out, DATA_A[1], DATA_B[1]);
  xnor xnor_3 (xnor_3_out, DATA_A[2], DATA_B[2]);
  xnor xnor_4 (xnor_4_out, DATA_A[3], DATA_B[3]);
  and and_1 (RESULT, xnor_1_out, xnor_2_out, xnor_3_out, xnor_4_out);
endmodule

// 3x_comp_4b
module comparator_triple_4b (
  input  [3:0] FIRST_A,
  input  [3:0] FIRST_B,
  input  [3:0] SECOND_A,
  input  [3:0] SECOND_B,
  input  [3:0] THIRD_A,
  input  [3:0] THIRD_B,
  input  ENABLE,
  output EQUALITY
);

  wire comparator_4b_1_result, comparator_4b_2_result, comparator_4b_3_result;

  comparator_4b comparator_4b_1 (.DATA_A(FIRST_A), .DATA_B(FIRST_B), .RESULT(comparator_4b_1_result));
  comparator_4b comparator_4b_2 (.DATA_A(SECOND_A), .DATA_B(SECOND_B), .RESULT(comparator_4b_2_result));
  comparator_4b comparator_4b_3 (.DATA_A(THIRD_A), .DATA_B(THIRD_B), .RESULT(comparator_4b_3_result));
  and and_1 (EQUALITY, comparator_4b_1_result, comparator_4b_2_result, comparator_4b_3_result, ENABLE);
endmodule

module single_ssd_with_3_outputs (
  input  [6:0] FIRST,
  input  [6:0] SECOND,
  input  [6:0] THIRD,
  input  [1:0] SELECTOR,
  output [6:0] SSD_OUTPUT
);

  Multiplexer #(.select(2), .width(7)) multiplexer_1 (
    .in0(FIRST), .in1(SECOND), .in2(THIRD), .in3(THIRD), .out(SSD_OUTPUT), .sel(SELECTOR));
endmodule

module triple_ssd_with_3_outputs (
  input  [6:0] FIRST_FIRST,
  input  [6:0] FIRST_SECOND,
  input  [6:0] FIRST_THIRD,
  input  [6:0] SECOND_FIRST,
  input  [6:0] SECOND_SECOND,
  input  [6:0] SECOND_THIRD,
  input  [6:0] THIRD_FIRST,
  input  [6:0] THIRD_SECOND,
  input  [6:0] THIRD_THIRD,
  input  [1:0] SELECTOR,
  output [6:0] FIRST_SSD_OUTPUT,
  output [6:0] SECOND_SSD_OUTPUT,
  output [6:0] THIRD_SSD_OUTPUT
);

  single_ssd_with_3_outputs single_ssd_with_3_outputs_1 (
    .FIRST(FIRST_FIRST), .SECOND(FIRST_SECOND), .THIRD(FIRST_THIRD), .SELECTOR(SELECTOR),
    .SSD_OUTPUT(FIRST_SSD_OUTPUT));
  single_ssd_with_3_outputs single_ssd_with_3_outputs_2 (
    .FIRST(SECOND_FIRST), .SECOND(SECOND_SECOND), .THIRD(SECOND_THIRD), .SELECTOR(SELECTOR),
    .SSD_OUTPUT(SECOND_SSD_OUTPUT));
  single_ssd_with_3_outputs single_ssd_with_3_outputs_3 (
    .FIRST(THIRD_FIRST), .SECOND(THIRD_SECOND), .THIRD(THIRD_THIRD), .SELECTOR(SELECTOR),
    .SSD_OUTPUT(THIRD_SSD_OUTPUT));
endmodule

module test_area (
);

  UE ue_1 ();  // open: DATA_IN, RESET_BUTTON, CLK, AVAILABLE, SSD_FIRST, SSD_SECOND, SSD_THIRD, BLOCKED
endmodule

module UC (
  input  [3:0] DATA_IN,
  input  RESET,
  input  CLOCK,
  input  [6:0] first_code,
  input  [6:0] second_code,
  input  [6:0] third_code,
  input  AVAILABLE_CODE,
  input  BLOCKED_CODE,
  output [3:0] DATA,
  output RST,
  output CLOCK_MAIN,
  output [6:0] first_ssd,
  output [6:0] second_ssd,
  output [6:0] third_ssd,
  output AVAILABLE_LED,
  output BLOCKED_LED
);


  assign AVAILABLE_LED = AVAILABLE_CODE;
  assign BLOCKED_LED = BLOCKED_CODE;
  assign CLOCK_MAIN = CLOCK;
  assign DATA = DATA_IN;
  assign first_ssd = first_code;
  assign RST = RESET;
  assign second_ssd = second_code;
  assign third_ssd = third_code;
endmodule

module main (
  input  [3:0] in_1
);

  wire button_1_out, clock_1_out, uc_1_available_led, uc_1_blocked_led, uc_1_clock_main, uc_1_rst,
       ue_1_available, ue_1_blocked;
  wire [3:0] uc_1_data;
  wire [6:0] uc_1_first_ssd, uc_1_second_ssd, uc_1_third_ssd, ue_1_ssd_first, ue_1_ssd_second, ue_1_ssd_third;

  Button button_1 (.out(button_1_out));
  Clock clock_1 (.out(clock_1_out));
  _7_Segment_Display FIRST_SSD (
    .g(uc_1_first_ssd[0]), .f(uc_1_first_ssd[1]), .a(uc_1_first_ssd[6]), .b(uc_1_first_ssd[5]),
    .e(uc_1_first_ssd[2]), .d(uc_1_first_ssd[3]), .c(uc_1_first_ssd[4]), .dp(1'b0));
  UC uc_1 (
    .DATA_IN(in_1), .RESET(button_1_out), .CLOCK(clock_1_out), .first_code(ue_1_ssd_first),
    .second_code(ue_1_ssd_second), .third_code(ue_1_ssd_third), .AVAILABLE_CODE(ue_1_available),
    .BLOCKED_CODE(ue_1_blocked), .DATA(uc_1_data), .RST(uc_1_rst), .CLOCK_MAIN(uc_1_clock_main),
    .first_ssd(uc_1_first_ssd), .second_ssd(uc_1_second_ssd), .third_ssd(uc_1_third_ssd),
    .AVAILABLE_LED(uc_1_available_led), .BLOCKED_LED(uc_1_blocked_led));
  _7_Segment_Display SECOND_SSD (
    .g(uc_1_second_ssd[0]), .f(uc_1_second_ssd[1]), .a(uc_1_second_ssd[6]), .b(uc_1_second_ssd[5]),
    .e(uc_1_second_ssd[2]), .d(uc_1_second_ssd[3]), .c(uc_1_second_ssd[4]), .dp(1'b0));
  _7_Segment_Display THIRD_LED (
    .g(uc_1_third_ssd[0]), .f(uc_1_third_ssd[1]), .a(uc_1_third_ssd[6]), .b(uc_1_third_ssd[5]),
    .e(uc_1_third_ssd[2]), .d(uc_1_third_ssd[3]), .c(uc_1_third_ssd[4]), .dp(1'b0));
  LED AVAILABLE (.in(uc_1_available_led));
  UE ue_1 (
    .DATA_IN(uc_1_data), .RESET_BUTTON(uc_1_rst), .CLK(uc_1_clock_main), .AVAILABLE(ue_1_available),
    .SSD_FIRST(ue_1_ssd_first), .SSD_SECOND(ue_1_ssd_second), .SSD_THIRD(ue_1_ssd_third),
    .BLOCKED(ue_1_blocked));
  LED BLOCKED (.in(uc_1_blocked_led));
endmodule

// VHDL entity hex_to_7seg, as the project stores it:
--------------------------------------------------------------------------------
-- Project : Cifru seif
-- File    :
-- Autor   : Luca-Andrei Codorean
-- Date    : 26.04.2023
--
--------------------------------------------------------------------------------
-- Description :
-- Se implementeaza un decodificator din cod binar, transmis pe 4 biti, in cod 
-- accesibil unui 7segment, capabil sa afiseze in format hexazecimal.
--------------------------------------------------------------------------------

LIBRARY ieee;
USE ieee.std_logic_1164.all;

ENTITY hex_to_7seg IS
  PORT (
  ------------------------------------------------------------------------------
  --Insert input ports below
  	hex_in: IN std_logic_vector(3 downto 0);
  	a_b_c_d_e_f_g: OUT std_logic_vector(6 downto 0)
    );
END hex_to_7seg;

--------------------------------------------------------------------------------
--Complete your VHDL description below
--------------------------------------------------------------------------------

ARCHITECTURE TypeArchitecture OF hex_to_7seg IS

BEGIN
	a_b_c_d_e_f_g <= 	not "0000001" when hex_in = x"0" else
					not "1001111" when hex_in = x"1" else
					not "0010010" when hex_in = x"2" else
					not "0000110" when hex_in = x"3" else
					not "1001100" when hex_in = x"4" else
					not "0100100" when hex_in = x"5" else
					not "0100000" when hex_in = x"6" else
					not "0001111" when hex_in = x"7" else
					not "0000000" when hex_in = x"8" else
					not "0000100" when hex_in = x"9" else
					not "0001000" when hex_in = x"A" else
					not "1100000" when hex_in = x"b" else
					not "0110001" when hex_in = x"C" else
					not "1000010" when hex_in = x"d" else
					not "0110000" when hex_in = x"E" else
					not "0111000" when hex_in = x"F" else
					not "1111111"; 					-- asta e cazul in care ledul este stins

END TypeArchitecture;

// VHDL entity MUX41, as the project stores it:
--------------------------------------------------------------------------------
-- Project : Cifru seif
-- File    :
-- Autor   : Dinca Diana
-- Date    : 27.04.2023
--
--------------------------------------------------------------------------------
-- Description :
-- Multiplexor 4 la 1, cu intrare pe 8bit, folosind instructiunea de asignare selectiva.
--------------------------------------------------------------------------------

LIBRARY ieee;
USE ieee.std_logic_1164.all;

ENTITY MUX41 IS
  PORT (
    I0      : IN  std_logic_vector(6 downto 0);                   
    I1      : IN  std_logic_vector(6 downto 0);                   
    I2      : IN  std_logic_vector(6 downto 0);                    
    I3      : IN  std_logic_vector(6 downto 0);                   
    S0      : IN  std_logic;
    S1      : IN  std_logic;
    Y       : OUT std_logic_vector(6 downto 0)                
    );
END MUX41;


ARCHITECTURE TypeArchitecture OF MUX41 IS

BEGIN

	Alegere: PROCESS (S0, S1)
	BEGIN
	CASE S0 is
		WHEN '0'=> IF S1= '0' 	THEN  Y<=I0;   --00
		         ELSIF S1= '1' 	THEN  Y<=I1;  	--01
		         END IF;
		WHEN '1'=> IF S1= '0' 	THEN  Y<=I2;   --10
		         ELSIF S1= '1' 	THEN  Y<=I3;   --11
		         END IF;
		when others => null;
	END CASE;
	END PROCESS Alegere;
	

END TypeArchitecture;

// VHDL entity flip_flop_d, as the project stores it:
--------------------------------------------------------------------------------
-- Project : Cifru seif
-- File    :
-- Autor   : Dinca Diana
-- Date    : 27.04.2023
--
--------------------------------------------------------------------------------
-- Description :
--
--------------------------------------------------------------------------------

LIBRARY ieee;
USE ieee.std_logic_1164.all;

ENTITY flip_flop_d IS
  PORT (
    D      : IN  std_logic;   
    CLK    : IN  std_logic;  
    CLR    : IN  std_logic;  
    Q      : OUT std_logic
    
    );
END flip_flop_d;


ARCHITECTURE TypeArchitecture OF flip_flop_d IS
BEGIN
	PROCESS (CLK, CLR)
	BEGIN
		IF CLK= '1' AND CLK'event then
		   Q<= D;
		END IF;
		IF CLR= '1' THEN
		   Q<= '0';
		END IF;
	END PROCESS ;
END TypeArchitecture;
